// Logisim project ProjectMostRecent.circ as structural Verilog: 1 circuit, main circuit main
module main (
);

  wire dipswitch_1_sw1, dipswitch_1_sw2, dipswitch_1_sw3, dipswitch_1_sw4, or_1_out, or_2_out, or_3_out,
       or_4_out, or_5_out, or_6_out, or_7_out, undriven, undriven_2, undriven_3, undriven_4, undriven_5,
       undriven_6, undriven_7, undriven_8, undriven_9;

  DipSwitch #(.number(4)) dipswitch_1 (
    .sw1(dipswitch_1_sw1), .sw2(dipswitch_1_sw2), .sw3(dipswitch_1_sw3), .sw4(dipswitch_1_sw4));
  LedBar #(.matrixcols(4)) ledbar_1 (
    .led0(dipswitch_1_sw1), .led1(dipswitch_1_sw2), .led2(dipswitch_1_sw3), .led3(dipswitch_1_sw4));
  or or_1 (or_1_out, undriven_4, undriven_5, undriven_6, undriven_8, undriven_9);
  or or_2 (or_2_out, undriven_2, undriven_4, undriven_3, undriven_5, undriven_6, undriven_8, undriven_9);
  _7_Segment_Display u_7_segment_display_1 (
    .g(or_2_out), .f(or_1_out), .a(or_5_out), .b(or_6_out), .e(or_3_out), .d(or_4_out), .c(or_7_out));  // open: dp
  or or_3 (or_3_out, undriven_2, undriven_6, undriven_8);
  or or_4 (or_4_out, undriven_2, undriven_3, undriven_5, undriven_6, undriven_8, undriven_9);
  or or_5 (or_5_out, undriven_2, undriven_3, undriven_5, undriven_6, undriven_7, undriven_8, undriven_9);
  or or_6 (or_6_out, undriven, undriven_2, undriven_3, undriven_4, undriven_7, undriven_8, undriven_9);
  or or_7 (or_7_out, undriven, undriven_3, undriven_4, undriven_5, undriven_6, undriven_7, undriven_8, undriven_9);
endmodule
