// Logisim project BranchForBCD.circ as structural Verilog: 2 circuits, main circuit main
module main (
);

  wire dipswitch_1_sw1, dipswitch_1_sw2, dipswitch_1_sw3, dipswitch_1_sw4, n7442_1_pin2, n7442_1_pin3,
       n7442_1_pin4, n7442_1_pin5, n7442_1_pin6, n7442_1_pin7, n7442_1_pin9, n7442_1_pin10, n7442_1_pin11,
       not_1_out, not_2_out, not_3_out, not_4_out, not_5_out, not_6_out, not_7_out, not_8_out, not_9_out,
       or_1_out, or_2_out, or_3_out, or_4_out, or_5_out, or_6_out, or_7_out;

  DipSwitch #(.number(4)) dipswitch_1 (
    .sw1(dipswitch_1_sw1), .sw2(dipswitch_1_sw2), .sw3(dipswitch_1_sw3), .sw4(dipswitch_1_sw4));
  LedBar #(.matrixcols(4)) ledbar_1 (
    .led0(dipswitch_1_sw1), .led1(dipswitch_1_sw2), .led2(dipswitch_1_sw3), .led3(dipswitch_1_sw4));
  _7442 #(.ShowInternalStructure("true")) u_7442_1 (
    .pin2(n7442_1_pin2), .pin3(n7442_1_pin3), .pin4(n7442_1_pin4), .pin5(n7442_1_pin5), .pin6(n7442_1_pin6),
    .pin7(n7442_1_pin7), .pin15(dipswitch_1_sw4), .pin14(dipswitch_1_sw3), .pin13(dipswitch_1_sw2),
    .pin12(dipswitch_1_sw1), .pin11(n7442_1_pin11), .pin10(n7442_1_pin10), .pin9(n7442_1_pin9));  // open: pin1
  not not_1 (not_1_out, n7442_1_pin2);
  not not_2 (not_2_out, n7442_1_pin3);
  not not_3 (not_3_out, n7442_1_pin4);
  not not_4 (not_4_out, n7442_1_pin11);
  not not_5 (not_5_out, n7442_1_pin10);
  not not_6 (not_6_out, n7442_1_pin9);
  not not_7 (not_7_out, n7442_1_pin5);
  not not_8 (not_8_out, n7442_1_pin6);
  not not_9 (not_9_out, n7442_1_pin7);
  or or_1 (or_1_out, not_7_out, not_8_out, not_9_out, not_5_out, not_4_out);
  or or_2 (or_2_out, not_2_out, not_7_out, not_3_out, not_8_out, not_9_out, not_5_out, not_4_out);
  _7_Segment_Display #(.decimalPoint("false")) u_7_segment_display_1 (
    .g(or_2_out), .f(or_1_out), .a(or_5_out), .b(or_6_out), .e(or_3_out), .d(or_4_out), .c(or_7_out));
  or or_3 (or_3_out, not_2_out, not_9_out, not_5_out);
  or or_4 (or_4_out, not_2_out, not_3_out, not_8_out, not_9_out, not_5_out, not_4_out);
  or or_5 (or_5_out, not_2_out, not_3_out, not_8_out, not_9_out, not_6_out, not_5_out, not_4_out);
  or or_6 (or_6_out, not_1_out, not_2_out, not_3_out, not_7_out, not_6_out, not_5_out, not_4_out);
  or or_7 (or_7_out, not_1_out, not_3_out, not_7_out, not_8_out, not_9_out, not_6_out, not_5_out, not_4_out);
endmodule

module BCD (
);

  wire and_1_out, and_2_out, and_3_out, and_4_out, and_5_out, and_6_out, and_7_out, and_8_out, and_9_out,
       and_10_out, and_11_out, and_12_out, and_13_out, and_14_out, and_15_out, and_16_out, and_17_out,
       and_18_out, buffer_1_out, buffer_2_out, dipswitch_1_sw5, dipswitch_1_sw6, dipswitch_1_sw7,
       dipswitch_1_sw8, nand_1_out, nand_2_out, nand_3_out, nand_4_out, nand_5_out, nand_6_out, nand_7_out,
       nand_8_out, nand_9_out, nor_1_out, nor_2_out, nor_3_out, nor_4_out, nor_5_out, nor_6_out, nor_7_out,
       not_1_out;

  DipSwitch dipswitch_1 (
    .sw5(dipswitch_1_sw5), .sw6(dipswitch_1_sw6), .sw7(dipswitch_1_sw7), .sw8(dipswitch_1_sw8));  // open: sw1, sw2, sw3, sw4
  _7442 #(.ShowInternalStructure("true")) u_7442_1 (
    .pin15(dipswitch_1_sw5), .pin14(dipswitch_1_sw6), .pin13(dipswitch_1_sw7), .pin12(dipswitch_1_sw8));  // open: pin1, pin2, pin3, pin4, pin5, pin6, pin7, pin11, pin10, pin9
  nand nand_1 (nand_1_out, dipswitch_1_sw5, buffer_1_out);
  nand nand_2 (nand_2_out, dipswitch_1_sw6, buffer_1_out);
  nand nand_3 (nand_3_out, dipswitch_1_sw7, buffer_1_out);
  nand nand_4 (nand_4_out, dipswitch_1_sw8, dipswitch_1_sw8);
  // Buffer buffer_1 has open pins: in=open, out=buffer_1_out
  not not_1 (not_1_out, 1'b1);
  buf buffer_2 (buffer_2_out, nand_5_out);
  nand nand_5 (nand_5_out, buffer_1_out, not_1_out, nand_4_out, nand_3_out, nand_2_out, nand_1_out);
  nand nand_6 (nand_6_out, nand_1_out, buffer_2_out);
  nand nand_7 (nand_7_out, nand_2_out, buffer_2_out);
  nand nand_8 (nand_8_out, nand_3_out, buffer_2_out);
  nand nand_9 (nand_9_out, nand_4_out, buffer_2_out);
  and and_1 (and_1_out, nand_7_out, nand_9_out);
  and and_2 (and_2_out, nand_1_out, nand_8_out);
  and and_3 (and_3_out, nand_6_out, nand_2_out, nand_3_out, nand_4_out);
  and and_4 (and_4_out, nand_7_out, nand_9_out);
  and and_5 (and_5_out, nand_6_out, nand_2_out, nand_8_out);
  and and_6 (and_6_out, nand_1_out, nand_7_out, nand_8_out);
  and and_7 (and_7_out, nand_8_out, nand_9_out);
  and and_8 (and_8_out, nand_1_out, nand_7_out, nand_3_out);
  and and_9 (and_9_out, nand_6_out, nand_2_out, nand_3_out);
  and and_10 (and_10_out, nand_1_out, nand_2_out, nand_8_out);
  and and_11 (and_11_out, nand_6_out, nand_7_out, nand_8_out);
  and and_12 (and_12_out, nand_6_out, nand_6_out);
  and and_13 (and_13_out, nand_2_out, nand_8_out);
  and and_14 (and_14_out, nand_6_out, nand_7_out);
  and and_15 (and_15_out, nand_7_out, nand_3_out);
  and and_16 (and_16_out, nand_6_out, nand_3_out, nand_4_out);
  and and_17 (and_17_out, nand_6_out, nand_7_out, nand_8_out);
  and and_18 (and_18_out, nand_2_out, nand_3_out, nand_4_out, buffer_1_out);
  nor nor_1 (nor_1_out, and_1_out, and_2_out, and_3_out);
  nor nor_2 (nor_2_out, and_4_out, and_5_out, and_6_out);
  nor nor_3 (nor_3_out, and_7_out, and_8_out);
  nor nor_4 (nor_4_out, and_9_out, and_10_out, and_11_out);
  nor nor_5 (nor_5_out, and_12_out, and_13_out);
  nor nor_6 (nor_6_out, and_14_out, and_15_out, and_16_out);
  nor nor_7 (nor_7_out, and_17_out, and_18_out);
  _7_Segment_Display #(.decimalPoint("false")) u_7_segment_display_1 (
    .g(nor_7_out), .f(nor_6_out), .a(nor_1_out), .b(nor_2_out), .e(nor_5_out), .d(nor_4_out), .c(nor_3_out));
endmodule
