// Logisim project ProjectMidSave.circ as structural Verilog: 1 circuit, main circuit main
module main (
);

  wire dipswitch_1_sw1, dipswitch_1_sw2, dipswitch_1_sw3, dipswitch_1_sw4, dipswitch_1_sw5, dipswitch_1_sw6,
       dipswitch_1_sw7, dipswitch_1_sw8, n7442_1_pin2, n7442_1_pin3, n7442_1_pin4, n7442_1_pin5,
       n7442_1_pin6, n7442_1_pin7, n7442_1_pin9, n7442_1_pin10, n7442_1_pin11, not_1_out, not_2_out,
       not_3_out, not_4_out, not_5_out, not_6_out, not_7_out, not_8_out, not_9_out, or_1_out, or_2_out,
       or_3_out, or_4_out, or_5_out, or_6_out, or_7_out;

  DipSwitch dipswitch_1 (
    .sw1(dipswitch_1_sw1), .sw2(dipswitch_1_sw2), .sw3(dipswitch_1_sw3), .sw4(dipswitch_1_sw4),
    .sw5(dipswitch_1_sw5), .sw6(dipswitch_1_sw6), .sw7(dipswitch_1_sw7), .sw8(dipswitch_1_sw8));
  LedBar ledbar_1 (
    .led0(dipswitch_1_sw1), .led1(dipswitch_1_sw2), .led2(dipswitch_1_sw3), .led3(dipswitch_1_sw4),
    .led4(dipswitch_1_sw5), .led5(dipswitch_1_sw6), .led6(dipswitch_1_sw7), .led7(dipswitch_1_sw8));
  _7_Segment_Display u_7_segment_display_1 (
    .g(dipswitch_1_sw5), .f(dipswitch_1_sw6), .a(dipswitch_1_sw7), .b(dipswitch_1_sw8), .e(dipswitch_1_sw4),
    .d(dipswitch_1_sw3), .c(dipswitch_1_sw2), .dp(dipswitch_1_sw1));
  _7442 #(.ShowInternalStructure("true")) u_7442_1 (
    .pin2(n7442_1_pin2), .pin3(n7442_1_pin3), .pin4(n7442_1_pin4), .pin5(n7442_1_pin5), .pin6(n7442_1_pin6),
    .pin7(n7442_1_pin7), .pin15(dipswitch_1_sw8), .pin14(dipswitch_1_sw7), .pin13(dipswitch_1_sw6),
    .pin12(dipswitch_1_sw5), .pin11(n7442_1_pin11), .pin10(n7442_1_pin10), .pin9(n7442_1_pin9));  // open: pin1
  not not_1 (not_1_out, n7442_1_pin2);
  not not_2 (not_2_out, n7442_1_pin3);
  not not_3 (not_3_out, n7442_1_pin4);
  not not_4 (not_4_out, n7442_1_pin11);
  not not_5 (not_5_out, n7442_1_pin10);
  not not_6 (not_6_out, n7442_1_pin9);
  not not_7 (not_7_out, n7442_1_pin5);
  not not_8 (not_8_out, n7442_1_pin6);
  not not_9 (not_9_out, n7442_1_pin7);
  or or_1 (or_1_out, not_7_out, not_8_out, not_9_out, not_5_out, not_4_out);
  or or_2 (or_2_out, not_2_out, not_7_out, not_3_out, not_8_out, not_9_out, not_5_out, not_4_out);
  _7_Segment_Display u_7_segment_display_2 (
    .g(or_2_out), .f(or_1_out), .a(or_5_out), .b(or_6_out), .e(or_3_out), .d(or_4_out), .c(or_7_out));  // open: dp
  or or_3 (or_3_out, not_2_out, not_9_out, not_5_out);
  or or_4 (or_4_out, not_2_out, not_3_out, not_8_out, not_9_out, not_5_out, not_4_out);
  or or_5 (or_5_out, not_2_out, not_3_out, not_8_out, not_9_out, not_6_out, not_5_out, not_4_out);
  or or_6 (or_6_out, not_1_out, not_2_out, not_3_out, not_7_out, not_6_out, not_5_out, not_4_out);
  or or_7 (or_7_out, not_1_out, not_3_out, not_7_out, not_8_out, not_9_out, not_6_out, not_5_out, not_4_out);
endmodule
